# Fritzing sketch HttpServer_W5500_Ethernet (saved by Fritzing 0.9.3b)
breadboards: 1

parts:
  Componente1 = Arduino Uno (Rev3) - ICSP  # not connected
  Componente2 = Arduino Ethernet Shield (Rev3)
  LED1 = LED - 5mm [color="Yellow (592nm)" package="5 mm [THT]"]
  R1 = Resistor [tolerance=±5% resistance=220 package=THT]
  U1 = POT [package=pot_mammoth]

nets:
  N1: Componente2.GND, R1.Pin_1, U1.E
  N2: Componente2.A0, U1.A
  N3: Componente2.PWM_D6, LED1.cathode
  N4: Componente2.5V, U1.S
  N5: LED1.anode, R1.Pin_0
