# Fritzing sketch YunSensorMote (saved by Fritzing 0.9.3b)

parts:
  Sunfounder2 = Analog Temeprature Sensor [package=THT]
  Componente1 = Arduino Yun
  Sunfounder1 = Humidity Sensor DHT11 [package=THT]
  Sunfounder3 = Lineal Hall Sensor Analog [package=THT]
  U1 = POT [package=pot_mammoth]
  Sunfounder4 = Relay module [package=THT]

nets:
  GND: Sunfounder2.GND, Componente1.GND, Sunfounder1.GND, Sunfounder4.GND
  VCC: Sunfounder2.Vcc, Componente1.5V, Sunfounder1.Vcc, Sunfounder3.Vout, U1.S, Sunfounder4.Vcc
  N1: Sunfounder2.Vout, Componente1.A0
  N2: Componente1.A1, Sunfounder1.Vout
  N3: Componente1.A2, Sunfounder3.Vcc
  N4: Componente1.A3, U1.A
  N5: Componente1.D8, Sunfounder4.Vout

notes:
  Temperature Sensor
  Humidity Sensor
  Hall Sensor
  Simulate any analog Sensor
  Relay Module

custom parts:
  Analog Temeprature Sensor: Analog Temeprature Sensor with thermistor for Sunfounder 37 Sensor Kit
  Humidity Sensor DHT11: Humidity Sensor DHT11 for Sunfounder 37 Sensor Kit
  Lineal Hall Sensor Analog: Lineal Hall Sensor Analog for Sunfounder 37 Sensor Kit
  Relay module: Relay Module for Sunfounder 37 Sensor Kit
