# Fritzing sketch ReadAnalogVoltage_sketch (saved by Fritzing 0.9.3b)
breadboards: 1

parts:
  Componente1 = Arduino Uno (Rev3) - ICSP
  U2 = POT [package=pot_alpha_rv16af-20]

nets:
  N1: Componente1.A0, U2.S
  N2: Componente1.5V, U2.E
  N3: Componente1.VIN, U2.A
