# Fritzing sketch tft-st3775-display (saved by Fritzing 0.9.3b)

parts:
  LCD1 = TFT 1.8 inch 160x128 w SD
  Part1 = Photon

nets:
  N1: LCD1.pin_1, Part1.VIN
  N2: LCD1.pin2, Part1.GND
  N3: LCD1.pin3, Part1.A2
  N4: LCD1.pin4, Part1.RST
  N5: LCD1.pin_5, Part1.D6
  N6: LCD1.pin_6, Part1.A5
  N7: LCD1.pin_7, Part1.A3
  N8: LCD1.pin_8, Part1.3V3

custom parts:
  TFT 1.8 inch 160x128 w SD: This is a generic 1.8 tft spi lcd display available on ebay and others. The 1.8" display has 128x160 color pixels.
